# Fritzing sketch schematic (saved by Fritzing 0.9.4)
circuit board: 8.46667cm x 5.64444cm
breadboards: 2

parts:
  Part1 = Arduino Uno (Rev3) - ICSP
  Q1 = NPN-Transistor [package="TO92 [THT]"]
  M1 = DC Motor
  M2 = DC Motor
  R1 = Resistor [tolerance=±5% resistance=220 package="0402 [SMD]"]
  VCC1 = Battery block 9V
  D1 = Rectifier Diode [package="Melf DO-213 AA [SMD]"]
  J1 = Basic Servo
  J2 = Basic Servo
  J3 = Basic Servo

nets:
  VCC: Part1.5V, J1.vcc, J2.vcc, J3.vcc
  GND: Part1.GND, Q1.E, VCC1.-, J1.gnd, J2.gnd, J3.gnd
  N1: Part1.D9_PWM, J1.pulse
  N2: Part1.D10_PWM/SS, J2.pulse
  N3: Part1.D11_PWM/MOSI, J3.pulse
  N4: Part1.D13/SCK, R1.Pin_1
  N5: Q1.B, R1.Pin_0
  N6: Q1.C, M1.pin_2, M2.pin_2, D1.anode
  N7: M1.pin_1, M2.pin_1, VCC1.+, D1.cathode

// code stored in the sketch: NSSentryGunBarrel.ino

